# Fritzing sketch Схема (saved by Fritzing 0.9.3b)
breadboards: 1

parts:
  Компонент1 = Arduino Uno (Rev3)
  U1 = NodeMCU V3.0
  DHT1 = DHT11 Humitidy and Temperature Sensor
  R1 = Photocell (LDR) [package=THT]
  R2 = Resistor [tolerance=±5% resistance=220 package=THT]
  R3 = Rotary Potentiometer (Small) [maximum_resistance=100kΩ package=THT]
  LED1 = LED - 5mm [color="Red (633nm)" package="5 mm [THT]"]
  R4 = Resistor [tolerance=±5% resistance=220 package=THT]

nets:
  N1: Компонент1.A0, R3.wiper
  N2: Компонент1.A1, R1.pin_1, R2.Pin_0
  N3: Компонент1.A4/SDA, U1.D1
  N4: Компонент1.A5/SCL, U1.D2
  N5: Компонент1.D5_PWM, DHT1.DATA
  5V: Компонент1.5V, DHT1.VDD, R1.pin_0, R3.leg2
  GND: Компонент1.GND, U1.GND, DHT1.GND, R2.Pin_1, R3.leg1, R4.Pin_0
  N6: U1.D3, LED1.anode
  N7: LED1.cathode, R4.Pin_1

custom parts:
  NodeMCU V3.0: ESP8266 based NodeMCU
  DHT11 Humitidy and Temperature Sensor: DHT11 Humidity and Temperature Sensor
